# Fritzing sketch DamiensCup (saved by Fritzing 0.9.3b)
circuit board: 6cm x 4cm
breadboards: 1

parts:
  ∞ = atmega328 [package=dip]
  R1 = Resistor [tolerance=±5% resistance=10k package=THT]
  J = Piezo Speaker
  C1 = Ceramic Capacitor [capacitance=22pF package="100 mil [THT, multilayer]"]
  C2 = Ceramic Capacitor [capacitance=22pF package="100 mil [THT, multilayer]"]
  XTAL = Crystal [frequency="16 Mhz" package=THT]
  R2 = Resistor [tolerance=±5% resistance=220 package=THT]
  R3 = Resistor [tolerance=±5% resistance=220 package=THT]
  R4 = Resistor [tolerance=±5% resistance=220 package=THT]
  LED = RGB LED (com. cathode, rgb) [package="5 mm [THT]"]
  TMP = TMP006 Thermopile Sensor
  -> = Adafruit MMA8451 Accelerometer [part_number="Adafruit #2019"]
  ≡ = Mini Lipo

nets:
  N1: ∞.RESET, R1.Pin_1
  N2: ∞.D3_(PWM), R2.Pin_0
  VCC: ∞.VCC, ∞.AVCC, ∞.AREF, TMP.VCC, ->.VIN, ≡.VBAT
  GND: ∞.GND, R1.Pin_0, J.pin1, C1.0, C2.0, LED.common_cathode, TMP.GND, ->.GND, ≡.GND
  N3: ∞.XLAT1, C1.1, XTAL.pin_0
  N4: ∞.XLAT2, C2.1, XTAL.pin_1
  N5: ∞.D5_(PWM), R3.Pin_0
  N6: ∞.D6_(PWM), R4.Pin_0
  N7: ∞.D12, J.pin2
  N8: ∞.A4, TMP.SCL, ->.SCL
  N9: ∞.A5, TMP.SDA, ->.SDA
  N10: R2.Pin_1, LED.blue_anode
  N11: R3.Pin_1, LED.green_anode
  N12: R4.Pin_1, LED.red_anode

notes:
  Damien's Coffee Cup
  2018 - Studio Laganne
  R
  G
  B
  -

custom parts:
  TMP006 Thermopile Sensor: Unlike all the other temperature sensors we have, this breakout has a really cool IR sensor from TI that can measure the temperature of an object without touching it! Simply point the sensor towards what you want to measure and it will detect the temperature by absorbing IR waves emitted. The embedded thermopile sensor generates a very very small voltage depending on how much IR there is, and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
  Adafruit MMA8451 Accelerometer: So many accelerometers and so little time! We've expanded our accelerometer selection even more with this high-precision and inexpensive MMA8451 Triple-Axis Accelerometer w/ 14-bit ADC. You can detect motion, tilt and basic orientation with a digital accelerometer - and the MMA8451 is a great accelerometer to start with. It has a wide usage range, from +-2g up to +-8g yet is easy to use with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
  Mini Lipo: Oh so handy, this little lipo charger is so small and easy to use you can keep it on your desk or mount it easily into any project! Simply plug it via any MiniUSB cable into a USB port and a 3.7V/4.2V lithium polymer or lithium ion rechargeable battery into the JST plug on the other end. There are two LEDs - one red and one green. While charging, the red LED is lit. When the battery is fully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
