# Fritzing sketch SMD (saved by Fritzing 0.9.3b)
circuit board: 1cm x 1cm
breadboards: 1

parts:
  Pad2 = Pad [width=0.14999999999999999 height=0.14999999999999999 connect=center]  # not connected
  Pad3 = Pad [width=0.14999999999999999 height=0.14999999999999999 connect=center]  # not connected
  Pad4 = Pad [width=0.14999999999999999 height=0.14999999999999999 connect=center]  # not connected
  Pad5 = Pad [width=0.14999999999999999 height=0.14999999999999999 connect=center]  # not connected
  Pad6 = Pad [width=0.14999999999999999 height=0.14999999999999999 connect=center]  # not connected
  Pad7 = Pad [width=0.14999999999999999 height=0.14999999999999999 connect=center]  # not connected
  Pad8 = Pad [width=0.14999999999999999 height=0.14999999999999999 connect=center]  # not connected
  Pad9 = Pad [width=0.14999999999999999 height=0.14999999999999999 connect=center]
  R1 = Resistor [tolerance=±5% resistance=220 package="0805 [SMD]"]

nets:
  N1: Pad9.pad, R1.Pin_1
